# Fritzing sketch diagrama1 (saved by Fritzing 0.9.3b)
breadboards: 1

parts:
  Raspberry_Pi_1 = Raspberry Pi 3 [part_number=RPI-3-V1.2]
  LED1 = smd LED [color="Red (633nm)" package="0603 [SMD]"]
  S1 = Momentary Switch [package=ksa_sealed_tac_switch]
  R1 = Resistor [tolerance=±5% resistance=220 package="0402 [SMD]"]

nets:
  N1: Raspberry_Pi_1.GIPO4, LED1.cathode
  N2: Raspberry_Pi_1.GIPO17, S1.1
  N3: Raspberry_Pi_1.GND, S1.3, R1.Pin_1
  N4: LED1.anode, R1.Pin_0

notes:
  GND (6)
  GPIO 17 (11)
  GPIO 4 (7)
  220Ohm
