# Fritzing sketch diagrama2 (saved by Fritzing 0.9.3b)
breadboards: 1

parts:
  Raspberry_Pi_1 = Raspberry Pi 3 [part_number=RPI-3-V1.2]
  J1 = Basic Servo
  hc-sr1 = hc-sr04
  R1 = Resistor [tolerance=±5% resistance=1k package="0402 [SMD]"]
  R2 = Resistor [tolerance=±5% resistance=2k package="0402 [SMD]"]

nets:
  GND: Raspberry_Pi_1.GND, J1.gnd, hc-sr1.GND, R2.Pin_1
  N1: Raspberry_Pi_1.GIPO24, R1.Pin_1, R2.Pin_0
  N2: Raspberry_Pi_1.GIPO23, hc-sr1.Trig
  N3: Raspberry_Pi_1.GIPO18, J1.pulse
  VCC: Raspberry_Pi_1.5V, J1.vcc, hc-sr1.VCC
  N4: hc-sr1.Echo, R1.Pin_0

notes:
  5v (2)
  GND (6)
  GPIO 18 (12)
  1kOhm
  2kOhm
  GPIO 24 (18)
  GPIO 23 (16)
