# Fritzing sketch diagrama3 (saved by Fritzing 0.9.3b)
breadboards: 1

parts:
  Raspberry_Pi_1 = Raspberry Pi 3 [part_number=RPI-3-V1.2]
  JP1 = Header 4 [package=molex-1x4_lock]
  R1 = Resistor [tolerance=±5% resistance=10k package="0402 [SMD]"]
  Sensore_PIR_HC-SR502 = HC-SR501 Body Sensor Module

nets:
  N1: Raspberry_Pi_1.3v3, JP1.4, R1.Pin_1
  N2: Raspberry_Pi_1.GIPO7, Sensore_PIR_HC-SR502.OUT
  N3: Raspberry_Pi_1.GIPO23, JP1.3, R1.Pin_0
  GND: Raspberry_Pi_1.GND, JP1.1, Sensore_PIR_HC-SR502.GND
  5V: Raspberry_Pi_1.5V, Sensore_PIR_HC-SR502.VCC

notes:
  3.3v (1)
  GND (6)
  DHT Frente
  GPIO 23 (16)
  10kOhm
  1kOhm
  5v (2)
  GPIO 7 (26)

custom parts:
  HC-SR501 Body Sensor Module: Pyroelectric Infrared PIR Motion Sensor Detector Module
