# Fritzing sketch esp8266_DHT22 (saved by Fritzing 0.9.4)
breadboards: 1

parts:
  U1 = ESP8266 WiFi Module [part_number=ESP8266]
  Part1 = Arduino Uno (Rev3) - ICSP
  R1 = Resistor [tolerance=±5% resistance=2.2k package="1206 [SMD]"]
  R2 = Resistor [tolerance=±5% resistance=1k package="1206 [SMD]"]
  S1 = Pushbutton [package="[THT]"]
  DHT2 = DHT22 Humidity and Temperature Sensor
  R3 = Resistor [tolerance=±5% resistance=10k package="2512 [SMD]"]

nets:
  N1: U1.RXD, Part1.D0/RX
  VCC: U1.VCC, Part1.3V3, DHT2.VDD, R3.Pin_0
  GND: U1.GPIO_0, U1.GND, Part1.GND, R1.Pin_0, S1.Pin_3, S1.Pin_4, DHT2.GND
  N2: U1.GPIO_2, DHT2.DATA, R3.Pin_1
  N3: U1.TXD, R1.Pin_1, R2.Pin_0
  N4: Part1.D1/TX, R2.Pin_1

notes:
  RX
  IO0
  RST
  TX
  2.2KOhm
  1KOhm
  VCC
  GND
  10KOhm
  IO2

custom parts:
  ESP8266 WiFi Module: Generic WiFi Module based on the ESP8266 with onboard PCB antenna and UART communications
