# Fritzing sketch esp8266 (saved by Fritzing 0.9.4)
breadboards: 1

parts:
  U1 = ESP8266 WiFi Module [part_number=ESP8266]
  Part1 = Arduino Uno (Rev3) - ICSP
  R1 = Resistor [tolerance=±5% resistance=2.2k package="1206 [SMD]"]
  R2 = Resistor [tolerance=±5% resistance=1k package="1206 [SMD]"]
  S1 = Pushbutton [package="[THT]"]

nets:
  N1: U1.RXD, Part1.D0/RX
  VCC: U1.VCC, Part1.3V3
  GND: U1.GPIO_0, U1.GND, Part1.GND, R1.Pin_0, S1.Pin_3, S1.Pin_4
  N2: U1.TXD, R1.Pin_1, R2.Pin_0
  N3: Part1.D1/TX, R2.Pin_1

notes:
  RX
  IO0
  RST
  TX
  2.2KOhm
  1KOhm
  VCC
  GND

custom parts:
  ESP8266 WiFi Module: Generic WiFi Module based on the ESP8266 with onboard PCB antenna and UART communications
