# Fritzing sketch ldr (saved by Fritzing 0.9.4)
breadboards: 1

parts:
  Part2 = Arduino Uno (Rev3) - ICSP
  R1 = Photocell (LDR) [package=THT]
  R2 = Resistor [tolerance=±5% resistance=220 package=THT]

nets:
  N1: Part2.A0, R1.pin_0, R2.Pin_1
  N2: Part2.5V, R1.pin_1
  N3: Part2.GND, R2.Pin_0
