# Fritzing sketch movimiento (saved by Fritzing 0.9.4)
breadboards: 1

parts:
  Raspberry_Pi_1 = Raspberry Pi 3 [part_number=RPI-3-V1.2]
  Part1 = HC-SR501 Body Sensor Module

nets:
  N1: Raspberry_Pi_1.GIPO18, Part1.OUT
  GND: Raspberry_Pi_1.GND, Part1.GND
  5V: Raspberry_Pi_1.5V, Part1.VCC

notes:
  5v (2)
  GND (6)
  GPIO 23 (16)

custom parts:
  HC-SR501 Body Sensor Module: Pyroelectric Infrared PIR Motion Sensor Detector Module
