# Fritzing sketch oled (saved by Fritzing 0.9.4)

parts:
  Raspberry_Pi_1 = Raspberry Pi 3 [part_number=RPI-3-V1.2]
  OLED1 = OLED 128x64 I2C Monochrome Display

nets:
  3V3: Raspberry_Pi_1.3v3, OLED1.VDD
  N1: Raspberry_Pi_1.GPIO2, OLED1.SDA
  N2: Raspberry_Pi_1.GPIO3, OLED1.SCK
  GND: Raspberry_Pi_1.GND, OLED1.GND
