# Fritzing sketch relay (saved by Fritzing 0.9.4)

parts:
  Raspberry_Pi_1 = Raspberry Pi 3 [part_number=RPI-3-V1.2]
  KY-1 = Keyes Relay [package=THT]

nets:
  N1: Raspberry_Pi_1.3v3, KY-1.power
  N2: Raspberry_Pi_1.GIPO23, KY-1.signal
  N3: Raspberry_Pi_1.GND, KY-1.ground

notes:
  GND (6)
  3.3V (1)
  GPIO 23(16)

custom parts:
  Keyes Relay: The Keyes 5V relay module is suitable for SCM development, home appliance control. It uses a 5V~12V TIL control signal which can control DC / AC signal.
