# Fritzing sketch temperatura (saved by Fritzing 0.9.4)
breadboards: 1

parts:
  Raspberry_Pi_1 = Raspberry Pi 3 [part_number=RPI-3-V1.2]  # not connected
  DHT1 = DHT22 Humidity and Temperature Sensor
  R1 = Resistor [tolerance=±5% resistance=10k package="2512 [SMD]"]

nets:
  N1: DHT1.VDD, R1.Pin_0
  N2: DHT1.DATA, R1.Pin_1

notes:
  GND (6)
  3.3V (1)
  GPIO 23(16)
  10KOhm
